# Fritzing sketch Domotica sketch (saved by Fritzing 0.9.3b)
breadboards: 1

parts:
  Componente1 = Arduino Mega 2560 (Rev3)
  Entrada_Garaje = RFID-RC522-v2
  Garaje = Basic Servo
  LED1 = RGB LED (com. cathode, rgb) [package="5 mm [THT]"]
  DHT1 = Humidity and Temperature Sensor DHT11
  Componente2 = Bluetooth HC-05 Macho  # not connected

nets:
  N1: Componente1.D8_PWM, LED1.red_anode
  5V: Componente1.5V, Entrada_Garaje.3.3V, Garaje.vcc
  GND: Componente1.GND, Entrada_Garaje.GND, Garaje.gnd
  N2: Componente1.D3_PWM, Garaje.pulse
  N3: Componente1.D5_PWM, Entrada_Garaje.RST
  N4: Componente1.D6_PWM, DHT1.Data-signal
  N5: Componente1.D7_PWM, LED1.blue_anode
  N6: Componente1.D50, Entrada_Garaje.MISO
  N7: Componente1.D51, Entrada_Garaje.MOSI
  N8: Componente1.D52, Entrada_Garaje.SCK
  N9: Componente1.D53, Entrada_Garaje.SDA

custom parts:
  RFID-RC522-v2: A simple China made RFID-RC522 Reader; do check the pin labels, as this is a MFRC522 based clone.
  Humidity and Temperature Sensor DHT11: Digital relative humidity & temperature sensor DHT11
